# Fritzing sketch dryer - fritzing (saved by Fritzing 1.0.1rc)

parts:
  Mod1 = Amica NodeMCU DEVKIT 1.0
  Деталь1 = TXB0108 8-channel Bi-directional Logic Level Converter
  Inner_sensor = DHT11 Humitidy and Temperature Sensor
  Outer_sensor = DHT11 Humitidy and Temperature Sensor
  UPS_250-300W = ATX24 Pin Power Supply Connector [package=atx24_right_angle]
  PowerOnOff = SWITCH-SPST-2 [package=switch-spst-vertical]
  Heater-Mosfet = MOSFET-NCHANNEL [part_number=IRLZ44N package=to220v]
  Heater = Inductor [part_number=40W-12V package="400 mil [THT]"]
  R2 = Temperature Sensor (Thermistor) [thermistor_type=NTC part_number="NTC 10K" package=THT]
  R2_2 = Resistor [tolerance=±5% power=0.25W resistance=220 package=THT]
  R11 = Resistor [tolerance=±5% power=0.25W resistance=10k package=THT]
  J5 = male pin header, 3 pins [form="♂ (male)"]
  J3 = female pin header, 3 pins [form="♀ (female)"]
  J2 = female pin header, 3 pins [form="♀ (female)"]
  J4 = male pin header, 3 pins [form="♂ (male)"]
  R12 = Resistor [tolerance=±5% power=0.25W resistance=10k package=THT]
  R13 = Resistor [tolerance=±5% power=0.25W resistance=10k package=THT]
  R14 = Resistor [tolerance=±5% resistance=10k power=0.25W package=THT]
  R15 = Resistor [tolerance=±5% resistance=10 power=0.25W package=THT]
  R16 = Resistor [tolerance=±5% resistance=1k power=0.25W package=THT]
  Start-Stop_btn = Square Pushbutton
  Heater_2 = LED - 3mm [color="Red (635nm)" current=0.030A package="3 mm [THT]"]
  R20 = Resistor [tolerance=±5% resistance=220 power=0.25W package=THT]
  Error = LED - 3mm [color="Orange (612nm)" current=0.030A package="3 mm [THT]"]
  Initialization = LED - 3mm [color="Blue (470nm)" current=0.030A package="3 mm [THT]"]
  Wi-Fi = LED - 3mm [color="Green (565nm)" current=0.030A package="3 mm [THT]"]
  R21 = Resistor [tolerance=±5% power=0.25W resistance=220 package=THT]
  R22 = Resistor [tolerance=±5% power=0.25W resistance=220 package=THT]
  J6 = female pin header, 2 pins [form="♀ (female)"]
  J7 = male pin header, 2 pins [form="♂ (male)"]
  1n4007 = Diode [package=diode-1n4001]
  PN2222 = NPN-Transistor [package="TO92 [THT]"]
  Fan_3-pin = Fan - Ventilador [package=THT]
  100nF = Capacitor [package=cap-pth-small2]

nets:
  GND: Mod1.pin2, Mod1.pin_9, Mod1.pin_25, Mod1.pin_29, Деталь1.GND, UPS_250-300W.GND, PowerOnOff.P, Heater-Mosfet.S, R2_2.Pin_1, R11.Pin_1, J3.pin3, J2.pin3, R14.Pin_1, Start-Stop_btn.leg1, R20.Pin_1, R21.Pin_1, R22.Pin_1, PN2222.E, 100nF.2
  N1: Mod1.pin5, Деталь1.A6
  N2: Mod1.pin6, Деталь1.A8
  N3: Mod1.pin7, Деталь1.A5
  N4: Mod1.pin8, Деталь1.A7
  N5: Mod1.pin_11, Start-Stop_btn.leg0
  N6: Mod1.pin_12, Деталь1.A2
  N7: Mod1.pin_13, Деталь1.A4
  N8: Mod1.pin_14, Деталь1.A1
  N9: Mod1.pin_15, Деталь1.A3
  N10: Mod1.pin_16, R11.Pin_0, J6.pin1
  N11: Mod1.pin_30, Деталь1.VCCB, UPS_250-300W.5V, J3.pin1, J2.pin1, R12.Pin_0, R13.Pin_0, J6.pin2
  N12: Деталь1.B1, R15.Pin_1
  N13: Деталь1.B2, J3.pin2, R12.Pin_1
  N14: Деталь1.B3, Heater_2.anode
  N15: Деталь1.B4, Wi-Fi.anode
  N16: Деталь1.B5, Error.anode
  N17: Деталь1.B6, Initialization.anode
  N18: Деталь1.B7, R16.Pin_1
  N19: Деталь1.B8, J2.pin2, R13.Pin_1
  N20: Деталь1.VCCA, UPS_250-300W.3.3V
  N21: Inner_sensor.VDD, J4.pin3
  N22: Inner_sensor.DATA, J4.pin2
  N23: Inner_sensor.GND, J4.pin1
  N24: Outer_sensor.VDD, J5.pin3
  N25: Outer_sensor.DATA, J5.pin2
  N26: Outer_sensor.GND, J5.pin1
  12V: UPS_250-300W.12V, Heater.pin_0, 1n4007.C, Fan_3-pin.5V
  N27: UPS_250-300W.PS_ON, PowerOnOff.O
  N28: Heater-Mosfet.G, R14.Pin_0, R15.Pin_0
  N29: Heater-Mosfet.D, Heater.pin_1
  N30: R2.pin_0, J7.pin2
  N31: R2.pin_1, J7.pin1
  N32: R2_2.Pin_0, Wi-Fi.cathode
  N33: R16.Pin_0, PN2222.B, 100nF.1
  N34: Heater_2.cathode, R20.Pin_0
  N35: Error.cathode, R21.Pin_0
  N36: Initialization.cathode, R22.Pin_0
  N37: 1n4007.A, PN2222.C, Fan_3-pin.GND

notes:
  1
  2
  3

custom parts:
  TXB0108 8-channel Bi-directional Logic Level Converter: Because the Arduino (and Basic Stamp) are 5V devices, and most modern sensors, displays, flash cards and modes are 3.3V-only, many makers find that they need to perform level shifting/conversion to protect the 3.3V device from 5V. Although one can use resistors to make a divider, for high speed transfers, the resistors can add a lot of slew and cause havoc that is tough to debug. For that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
  DHT11 Humitidy and Temperature Sensor: DHT11 Humidity and Temperature Sensor
  Fan - Ventilador: Ventilador de 2 pines, se encuentra comunmente en computadoras de escritorio
